# Fritzing sketch hackfest2015 (saved by Fritzing 0.9.2b)
perfboards: 6
breadboards: 1

parts:
  rp01 = Raspberry Pi 2
  ar01 = Arduino Mega 2560 (Rev3)
  casino_(lcd01) = 128 x 64 Graphic LCD
  R1 = Resistor [tolerance=±5% resistance=10k package=THT]
  LED2 = smd LED [color="Red (633nm)" package="0805 [SMD]"]
  R2 = Resistor [tolerance=±5% resistance=330 package=THT]
  pipeline_(lcd02) = 128 x 64 Graphic LCD  # not connected
  ar02 = Arduino Uno (Rev3) - ICSP
  solenoid01 = Solenoid  # not connected
  ar03 = Arduino Uno (Rev3) - ICSP
  VCC1 = Battery  # not connected

nets:
  N1: rp01.GPIO2, ar01.D20/SDA, ar02.A4/SDA, ar03.A4/SDA
  N2: rp01.GPIO3, ar01.D21/SCL, ar02.A5/SCL, ar03.A5/SCL
  GND: rp01.GND, ar01.GND, casino_(lcd01).1_Vss, casino_(lcd01).20_K(-), ar02.GND
  N3: ar01.D13_PWM, casino_(lcd01).6_Enable
  N4: ar01.D12_PWM, casino_(lcd01).5_R/W
  N5: ar01.D11_PWM, casino_(lcd01).4_D/I
  N6: ar01.D10_PWM, casino_(lcd01).3_Vo
  N7: ar01.D9_PWM, R1.Pin_1
  N8: ar01.D3_PWM, R2.Pin_1
  N9: LED2.anode, R2.Pin_0

// code stored in the sketch: test-lcd12864.ino
#include "U8glib.h" // Inclut la librairie U8G #include <IRremote.h> #define CONTRAST_PIN  10 #define BACKLIGHT_PIN 8 #define CONTRAST      125 #define LED_LIGHT_UP 0 #define LED_LIGHT_DOWN 1 #define LED_LIGHT_UP 2 #define LED_LIGHT_OFF 3 IRsend irsend;  //Default: pin 3 on Uno, 9 on Mega //U8GLIB_ST7920_128X64 u8g(8, 9, 10, 11, 4, 5, 6, 7, 18, U8G_PIN_NONE, U8G_PIN_NONE, 17, 16); // Câblage parallèle U8GLIB_ST7920_128X64 u8g(13, 12, 11, U8G_PIN_NONE); // Câblage SPI /* Fonction permettant de redessiner TOUT l'écran */ void draw(void) {   u8g.setFont(u8g_font_10x20); // Utilise la police de caractère standard   u8g.drawStr( 0, 22, "Hello World"); // Affiche hello world } void setModelLed(int action) {   unsigned long irCode;   switch (action) {     case LED_LIGHT_OFF: irCode = 0xF740BF;                         break;   }   Serial.print("Sending: ");   Serial.println(irCode,HEX);   irsend.sendNEC(irCode,32); } /* setup() */ void setup(void) {   Serial.begin(9600);   pinMode(CONTRAST_PIN, OUTPUT);   pinMode(BACKLIGHT_PIN, OUTPUT);   digitalWrite(BACKLIGHT_PIN, HIGH);   analogWrite(CONTRAST_PIN, CONTRAST);   u8g.setColorIndex(1); // Affichage en mode N&B (obligatoire vu que l'on a pas un écran couleur) } /* loop() */ void loop(void) {   u8g.firstPage(); // Sélectionne la 1er page mémoire de l'écran   do {     draw(); // Redessine tout l'écran   } while(u8g.nextPage()); // Sélectionne la page mémoire suivante   /* Delai avant de recommencer */   delay(1000);   setModelLed(LED_LIGHT_OFF); }
